// Logisim project test.circ as structural Verilog
module SR_latch (
  input  in_1,
  input  in_2,
  output out_3,
  output out_4
);

  wire not_1_out, not_2_out;

  not not_1 (not_1_out, in_1);
  not not_2 (not_2_out, in_2);
  nand nand_1 (out_3, not_1_out, out_4);
  nand nand_2 (out_4, out_3, not_2_out);
endmodule

module level_SR_flip_flop (
  input  S_D,
  input  S,
  input  C,
  input  R,
  input  R_D,
  output out_6,
  output out_7
);

  wire nand_1_out, nand_2_out, not_1_out, not_2_out;

  not not_1 (not_1_out, S_D);
  not not_2 (not_2_out, R_D);
  nand nand_1 (nand_1_out, S, C);
  nand nand_2 (nand_2_out, C, R);
  nand nand_3 (out_6, not_1_out, nand_1_out, out_7);
  nand nand_4 (out_7, out_6, nand_2_out, not_2_out);
endmodule

module level_D_flip_flop (
  input  S_D,
  input  D,
  input  C,
  input  R_D,
  output out_5,
  output out_6
);

  wire not_1_out;

  not not_1 (not_1_out, D);
  level_SR_flip_flop level_sr_flip_flop_1 (
    .S(D), .C(C), .out_6(out_5), .out_7(out_6), .R(not_1_out), .S_D(S_D), .R_D(R_D));
endmodule

module pulse_jk_latch (
  input  S_D,
  input  J,
  input  C,
  input  K,
  input  R_D,
  output out_6,
  output out_7
);

  wire and_1_out, and_2_out, level_sr_flip_flop_1_out_6, level_sr_flip_flop_1_out_7, not_1_out;

  and and_1 (and_1_out, out_7, J);
  and and_2 (and_2_out, K, out_6);
  level_SR_flip_flop level_sr_flip_flop_1 (
    .S(and_1_out), .C(C), .out_6(level_sr_flip_flop_1_out_6), .out_7(level_sr_flip_flop_1_out_7),
    .R(and_2_out), .S_D(S_D), .R_D(R_D));
  not not_1 (not_1_out, C);
  level_SR_flip_flop level_sr_flip_flop_2 (
    .S(level_sr_flip_flop_1_out_6), .C(not_1_out), .out_6(out_6), .out_7(out_7),
    .R(level_sr_flip_flop_1_out_7), .S_D(S_D), .R_D(R_D));
endmodule

module edge_D_flip_flop (
  input  S_D,
  input  D,
  input  C,
  input  R_D,
  output out_5,
  output out_6
);

  wire level_d_flip_flop_1_out_5, not_1_out, not_2_out;

  not not_1 (not_1_out, C);
  level_D_flip_flop level_d_flip_flop_1 (
    .S_D(S_D), .D(D), .C(not_1_out), .R_D(R_D), .out_5(level_d_flip_flop_1_out_5));  // open: out_6
  not not_2 (not_2_out, not_1_out);
  level_D_flip_flop level_d_flip_flop_2 (
    .S_D(S_D), .D(level_d_flip_flop_1_out_5), .C(not_2_out), .R_D(R_D), .out_5(out_5), .out_6(out_6));
endmodule

module edge_JK_flip_flop (
  input  S_D,
  input  J,
  input  C,
  input  K,
  input  R_D,
  output Q,
  output Q_prime
);

  wire and_1_out, and_2_out, not_1_out, or_1_out;

  not not_1 (not_1_out, K);
  and and_1 (and_1_out, J, Q_prime);
  and and_2 (and_2_out, not_1_out, Q);
  or or_1 (or_1_out, and_1_out, and_2_out);
  edge_D_flip_flop edge_d_flip_flop_1 (.S_D(S_D), .D(or_1_out), .C(C), .R_D(R_D), .out_5(Q), .out_6(Q_prime));
endmodule

module _2_4_decoder (
  input  Enable,
  input  A1,
  input  A0,
  output Y3,
  output Y2,
  output Y1,
  output Y0
);

  wire not_1_out, not_2_out, not_3_out, not_4_out;

  not not_1 (not_1_out, A0);
  not not_2 (not_2_out, A1);
  not not_3 (not_3_out, A1);
  not not_4 (not_4_out, A0);
  and and_1 (Y3, Enable, A1, A0);
  and and_2 (Y2, Enable, A1, not_1_out);
  and and_3 (Y1, Enable, not_2_out, A0);
  and and_4 (Y0, Enable, not_3_out, not_4_out);
endmodule

module _3_8_decoder (
  input  Enable,
  input  A2,
  input  A1,
  input  A0,
  output Y7,
  output Y6,
  output Y5,
  output Y4,
  output Y3,
  output Y2,
  output Y1,
  output Y0
);

  wire n2_4_decoder_1_y0, n2_4_decoder_1_y1, n2_4_decoder_1_y2, n2_4_decoder_1_y3, n2_4_decoder_2_y0,
       n2_4_decoder_2_y1, n2_4_decoder_2_y2, n2_4_decoder_2_y3, not_1_out;

  not not_1 (not_1_out, A2);
  _2_4_decoder u_2_4_decoder_1 (
    .Enable(A2), .A1(A1), .A0(A0), .Y3(n2_4_decoder_1_y3), .Y2(n2_4_decoder_1_y2), .Y1(n2_4_decoder_1_y1),
    .Y0(n2_4_decoder_1_y0));
  _2_4_decoder u_2_4_decoder_2 (
    .Enable(not_1_out), .A1(A1), .A0(A0), .Y3(n2_4_decoder_2_y3), .Y2(n2_4_decoder_2_y2),
    .Y1(n2_4_decoder_2_y1), .Y0(n2_4_decoder_2_y0));
  and and_1 (Y7, Enable, n2_4_decoder_1_y3);
  and and_2 (Y6, Enable, n2_4_decoder_1_y2);
  and and_3 (Y5, Enable, n2_4_decoder_1_y1);
  and and_4 (Y4, Enable, n2_4_decoder_1_y0);
  and and_5 (Y3, Enable, n2_4_decoder_2_y3);
  and and_6 (Y2, Enable, n2_4_decoder_2_y2);
  and and_7 (Y1, Enable, n2_4_decoder_2_y1);
  and and_8 (Y0, Enable, n2_4_decoder_2_y0);
endmodule

module _4_16_decoder (
  input  Enable,
  input  A3,
  input  A2,
  input  A1,
  input  A0,
  output Y15,
  output Y14,
  output Y13,
  output Y12,
  output Y11,
  output Y10,
  output Y9,
  output Y8,
  output Y7,
  output Y6,
  output Y5,
  output Y4,
  output Y3,
  output Y2,
  output Y1,
  output Y0
);

  wire n3_8_decoder_1_y0, n3_8_decoder_1_y1, n3_8_decoder_1_y2, n3_8_decoder_1_y3, n3_8_decoder_1_y4,
       n3_8_decoder_1_y5, n3_8_decoder_1_y6, n3_8_decoder_1_y7, n3_8_decoder_2_y0, n3_8_decoder_2_y1,
       n3_8_decoder_2_y2, n3_8_decoder_2_y3, n3_8_decoder_2_y4, n3_8_decoder_2_y5, n3_8_decoder_2_y6,
       n3_8_decoder_2_y7, not_1_out;

  not not_1 (not_1_out, A3);
  _3_8_decoder u_3_8_decoder_1 (
    .Enable(A3), .A2(A2), .A1(A1), .A0(A0), .Y7(n3_8_decoder_1_y7), .Y6(n3_8_decoder_1_y6),
    .Y5(n3_8_decoder_1_y5), .Y4(n3_8_decoder_1_y4), .Y3(n3_8_decoder_1_y3), .Y2(n3_8_decoder_1_y2),
    .Y1(n3_8_decoder_1_y1), .Y0(n3_8_decoder_1_y0));
  _3_8_decoder u_3_8_decoder_2 (
    .Enable(not_1_out), .A2(A2), .A1(A1), .A0(A0), .Y7(n3_8_decoder_2_y7), .Y6(n3_8_decoder_2_y6),
    .Y5(n3_8_decoder_2_y5), .Y4(n3_8_decoder_2_y4), .Y3(n3_8_decoder_2_y3), .Y2(n3_8_decoder_2_y2),
    .Y1(n3_8_decoder_2_y1), .Y0(n3_8_decoder_2_y0));
  and and_1 (Y15, Enable, n3_8_decoder_1_y7);
  and and_2 (Y14, Enable, n3_8_decoder_1_y6);
  and and_3 (Y13, Enable, n3_8_decoder_1_y5);
  and and_4 (Y12, Enable, n3_8_decoder_1_y4);
  and and_5 (Y11, Enable, n3_8_decoder_1_y3);
  and and_6 (Y10, Enable, n3_8_decoder_1_y2);
  and and_7 (Y9, Enable, n3_8_decoder_1_y1);
  and and_8 (Y8, Enable, n3_8_decoder_1_y0);
  and and_9 (Y7, Enable, n3_8_decoder_2_y7);
  and and_10 (Y6, Enable, n3_8_decoder_2_y6);
  and and_11 (Y5, Enable, n3_8_decoder_2_y5);
  and and_12 (Y4, Enable, n3_8_decoder_2_y4);
  and and_13 (Y3, Enable, n3_8_decoder_2_y3);
  and and_14 (Y2, Enable, n3_8_decoder_2_y2);
  and and_15 (Y1, Enable, n3_8_decoder_2_y1);
  and and_16 (Y0, Enable, n3_8_decoder_2_y0);
endmodule

module tmp_1_bit_memory (
  input  S_D,
  input  Enable,
  input  Data_Write,
  input  Clock,
  input  R_D,
  input  Write,
  input  Read,
  input  row_addr,
  input  clo_addr,
  output out_10
);

  wire and_1_out, and_2_out, level_sr_flip_flop_1_out_6, not_1_out;

  and and_1 (and_1_out, row_addr, clo_addr);
  and and_2 (and_2_out, Enable, Data_Write, and_1_out, Write);
  not not_1 (not_1_out, and_2_out);
  level_SR_flip_flop level_sr_flip_flop_1 (
    .S(and_2_out), .C(Clock), .out_6(level_sr_flip_flop_1_out_6), .R(not_1_out), .S_D(S_D), .R_D(R_D));  // open: out_7
  and and_3 (out_10, Enable, level_sr_flip_flop_1_out_6, and_1_out, Read);
endmodule

module _1_bit_memory (
  input  W,
  input  R,
  input  Date,
  input  row_addr,
  input  col_addr,
  input  Clock,
  input  S_D,
  input  R_D,
  output Output
);

  wire and_1_out, and_2_out, and_3_out, edge_jk_flip_flop_1_q, not_1_out;

  and and_1 (and_1_out, row_addr, col_addr);
  not not_1 (not_1_out, Date);
  and and_2 (and_2_out, W, W, Date, and_1_out);
  and and_3 (and_3_out, W, not_1_out, and_1_out);
  edge_JK_flip_flop edge_jk_flip_flop_1 (
    .S_D(S_D), .J(and_2_out), .K(and_3_out), .R_D(R_D), .Q(edge_jk_flip_flop_1_q), .C(Clock));  // open: Q_prime
  and and_4 (Output, and_1_out, R, edge_jk_flip_flop_1_q);
endmodule

module _8_8_bit_memory (
  input  Write,
  input  Read,
  input  Data_write,
  input  CLock,
  input  S_D,
  input  R_D,
  input  in_7,
  input  in_8,
  input  in_9,
  input  in_10,
  input  in_11,
  input  in_12,
  input  in_13,
  input  in_14,
  input  in_15,
  input  in_16,
  input  in_17,
  input  in_18,
  input  in_19,
  input  in_20,
  input  in_21,
  input  in_22,
  output Output
);

  wire n1_bit_memory_1_output, n1_bit_memory_2_output, n1_bit_memory_3_output, n1_bit_memory_4_output,
       n1_bit_memory_5_output, n1_bit_memory_6_output, n1_bit_memory_7_output, n1_bit_memory_8_output,
       n1_bit_memory_9_output, n1_bit_memory_10_output, n1_bit_memory_11_output, n1_bit_memory_12_output,
       n1_bit_memory_13_output, n1_bit_memory_14_output, n1_bit_memory_15_output, n1_bit_memory_16_output,
       n1_bit_memory_17_output, n1_bit_memory_18_output, n1_bit_memory_19_output, n1_bit_memory_20_output,
       n1_bit_memory_21_output, n1_bit_memory_22_output, n1_bit_memory_23_output, n1_bit_memory_24_output,
       n1_bit_memory_25_output, n1_bit_memory_26_output, n1_bit_memory_27_output, n1_bit_memory_28_output,
       n1_bit_memory_29_output, n1_bit_memory_30_output, n1_bit_memory_31_output, n1_bit_memory_32_output,
       n1_bit_memory_33_output, n1_bit_memory_34_output, n1_bit_memory_35_output, n1_bit_memory_36_output,
       n1_bit_memory_37_output, n1_bit_memory_38_output, n1_bit_memory_39_output, n1_bit_memory_40_output,
       n1_bit_memory_41_output, n1_bit_memory_42_output, n1_bit_memory_43_output, n1_bit_memory_44_output,
       n1_bit_memory_45_output, n1_bit_memory_46_output, n1_bit_memory_47_output, n1_bit_memory_48_output,
       n1_bit_memory_49_output, n1_bit_memory_50_output, n1_bit_memory_51_output, n1_bit_memory_52_output,
       n1_bit_memory_53_output, n1_bit_memory_54_output, n1_bit_memory_55_output, n1_bit_memory_56_output,
       n1_bit_memory_57_output, n1_bit_memory_58_output, n1_bit_memory_59_output, n1_bit_memory_60_output,
       n1_bit_memory_61_output, n1_bit_memory_62_output, n1_bit_memory_63_output, n1_bit_memory_64_output,
       or_1_out, or_2_out, or_3_out, or_4_out, or_5_out, or_6_out, or_7_out, or_8_out, or_9_out, or_10_out,
       or_11_out, or_13_out, or_14_out, or_15_out, or_16_out, or_17_out, or_18_out, or_19_out, or_20_out,
       or_21_out, or_22_out, or_23_out, or_24_out, or_25_out, or_26_out, or_27_out;

  _1_bit_memory u_1_bit_memory_1 (
    .W(Write), .R(Read), .Date(Data_write), .row_addr(in_7), .col_addr(in_15), .Clock(CLock),
    .Output(n1_bit_memory_1_output), .S_D(S_D), .R_D(R_D));
  _1_bit_memory u_1_bit_memory_2 (
    .W(Write), .R(Read), .Date(Data_write), .row_addr(in_8), .col_addr(in_15), .Clock(CLock),
    .Output(n1_bit_memory_2_output), .S_D(S_D), .R_D(R_D));
  _1_bit_memory u_1_bit_memory_3 (
    .W(Write), .R(Read), .Date(Data_write), .row_addr(in_9), .col_addr(in_15), .Clock(CLock),
    .Output(n1_bit_memory_3_output), .S_D(S_D), .R_D(R_D));
  _1_bit_memory u_1_bit_memory_4 (
    .W(Write), .R(Read), .Date(Data_write), .row_addr(in_10), .col_addr(in_15), .Clock(CLock),
    .Output(n1_bit_memory_4_output), .S_D(S_D), .R_D(R_D));
  _1_bit_memory u_1_bit_memory_5 (
    .W(Write), .R(Read), .Date(Data_write), .row_addr(in_11), .col_addr(in_15), .Clock(CLock),
    .Output(n1_bit_memory_5_output), .S_D(S_D), .R_D(R_D));
  _1_bit_memory u_1_bit_memory_6 (
    .W(Write), .R(Read), .Date(Data_write), .row_addr(in_12), .col_addr(in_15), .Clock(CLock),
    .Output(n1_bit_memory_6_output), .S_D(S_D), .R_D(R_D));
  _1_bit_memory u_1_bit_memory_7 (
    .W(Write), .R(Read), .Date(Data_write), .row_addr(in_13), .col_addr(in_15), .Clock(CLock),
    .Output(n1_bit_memory_7_output), .S_D(S_D), .R_D(R_D));
  _1_bit_memory u_1_bit_memory_8 (
    .W(Write), .R(Read), .Date(Data_write), .row_addr(in_14), .col_addr(in_15), .Clock(CLock),
    .Output(n1_bit_memory_8_output), .S_D(S_D), .R_D(R_D));
  or or_1 (or_1_out, n1_bit_memory_1_output, n1_bit_memory_2_output, n1_bit_memory_3_output, n1_bit_memory_4_output, n1_bit_memory_5_output);
  or or_2 (or_2_out, or_1_out, or_3_out);
  or or_3 (or_3_out, n1_bit_memory_6_output, n1_bit_memory_7_output, n1_bit_memory_8_output);
  _1_bit_memory u_1_bit_memory_9 (
    .W(Write), .R(Read), .Date(Data_write), .row_addr(in_7), .col_addr(in_16), .Clock(CLock),
    .Output(n1_bit_memory_9_output), .S_D(S_D), .R_D(R_D));
  _1_bit_memory u_1_bit_memory_10 (
    .W(Write), .R(Read), .Date(Data_write), .row_addr(in_8), .col_addr(in_16), .Clock(CLock),
    .Output(n1_bit_memory_10_output), .S_D(S_D), .R_D(R_D));
  _1_bit_memory u_1_bit_memory_11 (
    .W(Write), .R(Read), .Date(Data_write), .row_addr(in_9), .col_addr(in_16), .Clock(CLock),
    .Output(n1_bit_memory_11_output), .S_D(S_D), .R_D(R_D));
  _1_bit_memory u_1_bit_memory_12 (
    .W(Write), .R(Read), .Date(Data_write), .row_addr(in_10), .col_addr(in_16), .Clock(CLock),
    .Output(n1_bit_memory_12_output), .S_D(S_D), .R_D(R_D));
  _1_bit_memory u_1_bit_memory_13 (
    .W(Write), .R(Read), .Date(Data_write), .row_addr(in_11), .col_addr(in_16), .Clock(CLock),
    .Output(n1_bit_memory_13_output), .S_D(S_D), .R_D(R_D));
  _1_bit_memory u_1_bit_memory_14 (
    .W(Write), .R(Read), .Date(Data_write), .row_addr(in_12), .col_addr(in_16), .Clock(CLock),
    .Output(n1_bit_memory_14_output), .S_D(S_D), .R_D(R_D));
  _1_bit_memory u_1_bit_memory_15 (
    .W(Write), .R(Read), .Date(Data_write), .row_addr(in_13), .col_addr(in_16), .Clock(CLock),
    .Output(n1_bit_memory_15_output), .S_D(S_D), .R_D(R_D));
  _1_bit_memory u_1_bit_memory_16 (
    .W(Write), .R(Read), .Date(Data_write), .row_addr(in_14), .col_addr(in_16), .Clock(CLock),
    .Output(n1_bit_memory_16_output), .S_D(S_D), .R_D(R_D));
  or or_4 (or_4_out, n1_bit_memory_9_output, n1_bit_memory_10_output, n1_bit_memory_11_output, n1_bit_memory_12_output, n1_bit_memory_13_output);
  or or_5 (or_5_out, or_4_out, or_6_out);
  or or_6 (or_6_out, n1_bit_memory_14_output, n1_bit_memory_15_output, n1_bit_memory_16_output);
  _1_bit_memory u_1_bit_memory_17 (
    .W(Write), .R(Read), .Date(Data_write), .row_addr(in_7), .col_addr(in_17), .Clock(CLock),
    .Output(n1_bit_memory_17_output), .S_D(S_D), .R_D(R_D));
  _1_bit_memory u_1_bit_memory_18 (
    .W(Write), .R(Read), .Date(Data_write), .row_addr(in_8), .col_addr(in_17), .Clock(CLock),
    .Output(n1_bit_memory_18_output), .S_D(S_D), .R_D(R_D));
  _1_bit_memory u_1_bit_memory_19 (
    .W(Write), .R(Read), .Date(Data_write), .row_addr(in_9), .col_addr(in_17), .Clock(CLock),
    .Output(n1_bit_memory_19_output), .S_D(S_D), .R_D(R_D));
  _1_bit_memory u_1_bit_memory_20 (
    .W(Write), .R(Read), .Date(Data_write), .row_addr(in_10), .col_addr(in_17), .Clock(CLock),
    .Output(n1_bit_memory_20_output), .S_D(S_D), .R_D(R_D));
  _1_bit_memory u_1_bit_memory_21 (
    .W(Write), .R(Read), .Date(Data_write), .row_addr(in_11), .col_addr(in_17), .Clock(CLock),
    .Output(n1_bit_memory_21_output), .S_D(S_D), .R_D(R_D));
  _1_bit_memory u_1_bit_memory_22 (
    .W(Write), .R(Read), .Date(Data_write), .row_addr(in_12), .col_addr(in_17), .Clock(CLock),
    .Output(n1_bit_memory_22_output), .S_D(S_D), .R_D(R_D));
  _1_bit_memory u_1_bit_memory_23 (
    .W(Write), .R(Read), .Date(Data_write), .row_addr(in_13), .col_addr(in_17), .Clock(CLock),
    .Output(n1_bit_memory_23_output), .S_D(S_D), .R_D(R_D));
  _1_bit_memory u_1_bit_memory_24 (
    .W(Write), .R(Read), .Date(Data_write), .row_addr(in_14), .col_addr(in_17), .Clock(CLock),
    .Output(n1_bit_memory_24_output), .S_D(S_D), .R_D(R_D));
  or or_7 (or_7_out, or_2_out, or_5_out, or_8_out, or_13_out, or_16_out);
  or or_8 (or_8_out, or_9_out, or_10_out);
  or or_9 (or_9_out, n1_bit_memory_17_output, n1_bit_memory_18_output, n1_bit_memory_19_output, n1_bit_memory_20_output, n1_bit_memory_21_output);
  or or_10 (or_10_out, n1_bit_memory_22_output, n1_bit_memory_23_output, n1_bit_memory_24_output);
  _1_bit_memory u_1_bit_memory_25 (
    .W(Write), .R(Read), .Date(Data_write), .row_addr(in_7), .col_addr(in_18), .Clock(CLock),
    .Output(n1_bit_memory_25_output), .S_D(S_D), .R_D(R_D));
  _1_bit_memory u_1_bit_memory_26 (
    .W(Write), .R(Read), .Date(Data_write), .row_addr(in_8), .col_addr(in_18), .Clock(CLock),
    .Output(n1_bit_memory_26_output), .S_D(S_D), .R_D(R_D));
  _1_bit_memory u_1_bit_memory_27 (
    .W(Write), .R(Read), .Date(Data_write), .row_addr(in_9), .col_addr(in_18), .Clock(CLock),
    .Output(n1_bit_memory_27_output), .S_D(S_D), .R_D(R_D));
  _1_bit_memory u_1_bit_memory_28 (
    .W(Write), .R(Read), .Date(Data_write), .row_addr(in_10), .col_addr(in_18), .Clock(CLock),
    .Output(n1_bit_memory_28_output), .S_D(S_D), .R_D(R_D));
  _1_bit_memory u_1_bit_memory_29 (
    .W(Write), .R(Read), .Date(Data_write), .row_addr(in_11), .col_addr(in_18), .Clock(CLock),
    .Output(n1_bit_memory_29_output), .S_D(S_D), .R_D(R_D));
  _1_bit_memory u_1_bit_memory_30 (
    .W(Write), .R(Read), .Date(Data_write), .row_addr(in_12), .col_addr(in_18), .Clock(CLock),
    .Output(n1_bit_memory_30_output), .S_D(S_D), .R_D(R_D));
  _1_bit_memory u_1_bit_memory_31 (
    .W(Write), .R(Read), .Date(Data_write), .row_addr(in_13), .col_addr(in_18), .Clock(CLock),
    .Output(n1_bit_memory_31_output), .S_D(S_D), .R_D(R_D));
  _1_bit_memory u_1_bit_memory_32 (
    .W(Write), .R(Read), .Date(Data_write), .row_addr(in_14), .col_addr(in_18), .Clock(CLock),
    .Output(n1_bit_memory_32_output), .S_D(S_D), .R_D(R_D));
  or or_11 (or_11_out, n1_bit_memory_25_output, n1_bit_memory_26_output, n1_bit_memory_27_output, n1_bit_memory_28_output, n1_bit_memory_29_output);
  or or_12 (Output, or_7_out, or_23_out);
  or or_13 (or_13_out, or_11_out, or_14_out);
  or or_14 (or_14_out, n1_bit_memory_30_output, n1_bit_memory_31_output, n1_bit_memory_32_output);
  _1_bit_memory u_1_bit_memory_33 (
    .W(Write), .R(Read), .Date(Data_write), .row_addr(in_7), .col_addr(in_19), .Clock(CLock),
    .Output(n1_bit_memory_33_output), .S_D(S_D), .R_D(R_D));
  _1_bit_memory u_1_bit_memory_34 (
    .W(Write), .R(Read), .Date(Data_write), .row_addr(in_8), .col_addr(in_19), .Clock(CLock),
    .Output(n1_bit_memory_34_output), .S_D(S_D), .R_D(R_D));
  _1_bit_memory u_1_bit_memory_35 (
    .W(Write), .R(Read), .Date(Data_write), .row_addr(in_9), .col_addr(in_19), .Clock(CLock),
    .Output(n1_bit_memory_35_output), .S_D(S_D), .R_D(R_D));
  _1_bit_memory u_1_bit_memory_36 (
    .W(Write), .R(Read), .Date(Data_write), .row_addr(in_10), .col_addr(in_19), .Clock(CLock),
    .Output(n1_bit_memory_36_output), .S_D(S_D), .R_D(R_D));
  _1_bit_memory u_1_bit_memory_37 (
    .W(Write), .R(Read), .Date(Data_write), .row_addr(in_11), .col_addr(in_19), .Clock(CLock),
    .Output(n1_bit_memory_37_output), .S_D(S_D), .R_D(R_D));
  _1_bit_memory u_1_bit_memory_38 (
    .W(Write), .R(Read), .Date(Data_write), .row_addr(in_12), .col_addr(in_19), .Clock(CLock),
    .Output(n1_bit_memory_38_output), .S_D(S_D), .R_D(R_D));
  _1_bit_memory u_1_bit_memory_39 (
    .W(Write), .R(Read), .Date(Data_write), .row_addr(in_13), .col_addr(in_19), .Clock(CLock),
    .Output(n1_bit_memory_39_output), .S_D(S_D), .R_D(R_D));
  _1_bit_memory u_1_bit_memory_40 (
    .W(Write), .R(Read), .Date(Data_write), .row_addr(in_14), .col_addr(in_19), .Clock(CLock),
    .Output(n1_bit_memory_40_output), .S_D(S_D), .R_D(R_D));
  or or_15 (or_15_out, n1_bit_memory_33_output, n1_bit_memory_34_output, n1_bit_memory_35_output, n1_bit_memory_36_output, n1_bit_memory_37_output);
  or or_16 (or_16_out, or_15_out, or_17_out);
  or or_17 (or_17_out, n1_bit_memory_38_output, n1_bit_memory_39_output, n1_bit_memory_40_output);
  _1_bit_memory u_1_bit_memory_41 (
    .W(Write), .R(Read), .Date(Data_write), .row_addr(in_7), .col_addr(in_20), .Clock(CLock),
    .Output(n1_bit_memory_41_output), .S_D(S_D), .R_D(R_D));
  _1_bit_memory u_1_bit_memory_42 (
    .W(Write), .R(Read), .Date(Data_write), .row_addr(in_8), .col_addr(in_20), .Clock(CLock),
    .Output(n1_bit_memory_42_output), .S_D(S_D), .R_D(R_D));
  _1_bit_memory u_1_bit_memory_43 (
    .W(Write), .R(Read), .Date(Data_write), .row_addr(in_9), .col_addr(in_20), .Clock(CLock),
    .Output(n1_bit_memory_43_output), .S_D(S_D), .R_D(R_D));
  _1_bit_memory u_1_bit_memory_44 (
    .W(Write), .R(Read), .Date(Data_write), .row_addr(in_10), .col_addr(in_20), .Clock(CLock),
    .Output(n1_bit_memory_44_output), .S_D(S_D), .R_D(R_D));
  _1_bit_memory u_1_bit_memory_45 (
    .W(Write), .R(Read), .Date(Data_write), .row_addr(in_11), .col_addr(in_20), .Clock(CLock),
    .Output(n1_bit_memory_45_output), .S_D(S_D), .R_D(R_D));
  _1_bit_memory u_1_bit_memory_46 (
    .W(Write), .R(Read), .Date(Data_write), .row_addr(in_12), .col_addr(in_20), .Clock(CLock),
    .Output(n1_bit_memory_46_output), .S_D(S_D), .R_D(R_D));
  _1_bit_memory u_1_bit_memory_47 (
    .W(Write), .R(Read), .Date(Data_write), .row_addr(in_13), .col_addr(in_20), .Clock(CLock),
    .Output(n1_bit_memory_47_output), .S_D(S_D), .R_D(R_D));
  _1_bit_memory u_1_bit_memory_48 (
    .W(Write), .R(Read), .Date(Data_write), .row_addr(in_14), .col_addr(in_20), .Clock(CLock),
    .Output(n1_bit_memory_48_output), .S_D(S_D), .R_D(R_D));
  or or_18 (or_18_out, n1_bit_memory_41_output, n1_bit_memory_42_output, n1_bit_memory_43_output, n1_bit_memory_44_output, n1_bit_memory_45_output);
  or or_19 (or_19_out, or_18_out, or_20_out);
  or or_20 (or_20_out, n1_bit_memory_46_output, n1_bit_memory_47_output, n1_bit_memory_48_output);
  _1_bit_memory u_1_bit_memory_49 (
    .W(Write), .R(Read), .Date(Data_write), .row_addr(in_7), .col_addr(in_21), .Clock(CLock),
    .Output(n1_bit_memory_49_output), .S_D(S_D), .R_D(R_D));
  _1_bit_memory u_1_bit_memory_50 (
    .W(Write), .R(Read), .Date(Data_write), .row_addr(in_8), .col_addr(in_21), .Clock(CLock),
    .Output(n1_bit_memory_50_output), .S_D(S_D), .R_D(R_D));
  _1_bit_memory u_1_bit_memory_51 (
    .W(Write), .R(Read), .Date(Data_write), .row_addr(in_9), .col_addr(in_21), .Clock(CLock),
    .Output(n1_bit_memory_51_output), .S_D(S_D), .R_D(R_D));
  _1_bit_memory u_1_bit_memory_52 (
    .W(Write), .R(Read), .Date(Data_write), .row_addr(in_10), .col_addr(in_21), .Clock(CLock),
    .Output(n1_bit_memory_52_output), .S_D(S_D), .R_D(R_D));
  _1_bit_memory u_1_bit_memory_53 (
    .W(Write), .R(Read), .Date(Data_write), .row_addr(in_11), .col_addr(in_21), .Clock(CLock),
    .Output(n1_bit_memory_53_output), .S_D(S_D), .R_D(R_D));
  _1_bit_memory u_1_bit_memory_54 (
    .W(Write), .R(Read), .Date(Data_write), .row_addr(in_12), .col_addr(in_21), .Clock(CLock),
    .Output(n1_bit_memory_54_output), .S_D(S_D), .R_D(R_D));
  _1_bit_memory u_1_bit_memory_55 (
    .W(Write), .R(Read), .Date(Data_write), .row_addr(in_13), .col_addr(in_21), .Clock(CLock),
    .Output(n1_bit_memory_55_output), .S_D(S_D), .R_D(R_D));
  _1_bit_memory u_1_bit_memory_56 (
    .W(Write), .R(Read), .Date(Data_write), .row_addr(in_14), .col_addr(in_21), .Clock(CLock),
    .Output(n1_bit_memory_56_output), .S_D(S_D), .R_D(R_D));
  or or_21 (or_21_out, or_22_out, or_24_out);
  or or_22 (or_22_out, n1_bit_memory_49_output, n1_bit_memory_50_output, n1_bit_memory_51_output, n1_bit_memory_52_output, n1_bit_memory_53_output);
  or or_23 (or_23_out, or_19_out, or_21_out, or_25_out);
  or or_24 (or_24_out, n1_bit_memory_54_output, n1_bit_memory_55_output, n1_bit_memory_56_output);
  _1_bit_memory u_1_bit_memory_57 (
    .W(Write), .R(Read), .Date(Data_write), .row_addr(in_7), .col_addr(in_22), .Clock(CLock),
    .Output(n1_bit_memory_57_output), .S_D(S_D), .R_D(R_D));
  _1_bit_memory u_1_bit_memory_58 (
    .W(Write), .R(Read), .Date(Data_write), .row_addr(in_8), .col_addr(in_22), .Clock(CLock),
    .Output(n1_bit_memory_58_output), .S_D(S_D), .R_D(R_D));
  _1_bit_memory u_1_bit_memory_59 (
    .W(Write), .R(Read), .Date(Data_write), .row_addr(in_9), .col_addr(in_22), .Clock(CLock),
    .Output(n1_bit_memory_59_output), .S_D(S_D), .R_D(R_D));
  _1_bit_memory u_1_bit_memory_60 (
    .W(Write), .R(Read), .Date(Data_write), .row_addr(in_10), .col_addr(in_22), .Clock(CLock),
    .Output(n1_bit_memory_60_output), .S_D(S_D), .R_D(R_D));
  _1_bit_memory u_1_bit_memory_61 (
    .W(Write), .R(Read), .Date(Data_write), .row_addr(in_11), .col_addr(in_22), .Clock(CLock),
    .Output(n1_bit_memory_61_output), .S_D(S_D), .R_D(R_D));
  _1_bit_memory u_1_bit_memory_62 (
    .W(Write), .R(Read), .Date(Data_write), .row_addr(in_12), .col_addr(in_22), .Clock(CLock),
    .Output(n1_bit_memory_62_output), .S_D(S_D), .R_D(R_D));
  _1_bit_memory u_1_bit_memory_63 (
    .W(Write), .R(Read), .Date(Data_write), .row_addr(in_13), .col_addr(in_22), .Clock(CLock),
    .Output(n1_bit_memory_63_output), .S_D(S_D), .R_D(R_D));
  _1_bit_memory u_1_bit_memory_64 (
    .W(Write), .R(Read), .Date(Data_write), .row_addr(in_14), .col_addr(in_22), .Clock(CLock),
    .Output(n1_bit_memory_64_output), .S_D(S_D), .R_D(R_D));
  or or_25 (or_25_out, or_26_out, or_27_out);
  or or_26 (or_26_out, n1_bit_memory_57_output, n1_bit_memory_58_output, n1_bit_memory_59_output, n1_bit_memory_60_output, n1_bit_memory_61_output);
  or or_27 (or_27_out, n1_bit_memory_62_output, n1_bit_memory_63_output, n1_bit_memory_64_output);
endmodule

module _2_6_1_memory (
  input  Enable,
  input  R_D,
  input  S_D,
  input  Clock,
  input  Data_Write,
  input  Read,
  input  Write,
  input  A5,
  input  A4,
  input  A3,
  input  A2,
  input  A1,
  input  A0,
  output out_14
);

  wire and_1_out, n3_8_decoder_1_y0, n3_8_decoder_1_y1, n3_8_decoder_1_y2, n3_8_decoder_1_y3,
       n3_8_decoder_1_y4, n3_8_decoder_1_y5, n3_8_decoder_1_y6, n3_8_decoder_1_y7, n3_8_decoder_2_y0,
       n3_8_decoder_2_y1, n3_8_decoder_2_y2, n3_8_decoder_2_y3, n3_8_decoder_2_y4, n3_8_decoder_2_y5,
       n3_8_decoder_2_y6, n3_8_decoder_2_y7;

  buf and_1 (and_1_out, Enable);  // AND_Gate
  _3_8_decoder u_3_8_decoder_1 (
    .Enable(and_1_out), .A2(A5), .A1(A4), .A0(A3), .Y7(n3_8_decoder_1_y7), .Y6(n3_8_decoder_1_y6),
    .Y5(n3_8_decoder_1_y5), .Y4(n3_8_decoder_1_y4), .Y3(n3_8_decoder_1_y3), .Y2(n3_8_decoder_1_y2),
    .Y1(n3_8_decoder_1_y1), .Y0(n3_8_decoder_1_y0));
  _8_8_bit_memory u_8_8_bit_memory_1 (
    .Write(Write), .Read(Read), .Data_write(Data_Write), .CLock(Clock), .S_D(S_D), .R_D(R_D),
    .in_7(n3_8_decoder_1_y7), .in_8(n3_8_decoder_1_y6), .in_9(n3_8_decoder_1_y5), .in_10(n3_8_decoder_1_y4),
    .in_11(n3_8_decoder_1_y3), .in_12(n3_8_decoder_1_y2), .in_13(n3_8_decoder_1_y1),
    .in_14(n3_8_decoder_1_y0), .Output(out_14), .in_15(n3_8_decoder_2_y7), .in_16(n3_8_decoder_2_y6),
    .in_17(n3_8_decoder_2_y5), .in_18(n3_8_decoder_2_y4), .in_19(n3_8_decoder_2_y3),
    .in_20(n3_8_decoder_2_y2), .in_21(n3_8_decoder_2_y1), .in_22(n3_8_decoder_2_y0));
  _3_8_decoder u_3_8_decoder_2 (
    .Enable(and_1_out), .A2(A2), .A1(A1), .A0(A0), .Y7(n3_8_decoder_2_y7), .Y6(n3_8_decoder_2_y6),
    .Y5(n3_8_decoder_2_y5), .Y4(n3_8_decoder_2_y4), .Y3(n3_8_decoder_2_y3), .Y2(n3_8_decoder_2_y2),
    .Y1(n3_8_decoder_2_y1), .Y0(n3_8_decoder_2_y0));
endmodule

module _2_6_4_memory (
  input  Enable,
  input  R_D,
  input  S_D,
  input  Clock,
  input  Read,
  input  Write,
  input  [3:0] _4_bit_Data_input,
  input  [5:0] _6_bit_addr,
  output [3:0] _4_bit_Data_Output
);

  _2_6_1_memory u_2_6_1_memory_1 (
    .Enable(Enable), .A5(_6_bit_addr[5]), .A4(_6_bit_addr[4]), .A3(_6_bit_addr[3]), .A2(_6_bit_addr[2]),
    .A1(_6_bit_addr[1]), .A0(_6_bit_addr[0]), .R_D(R_D), .S_D(S_D), .Clock(Clock),
    .Data_Write(_4_bit_Data_input[3]), .Read(Read), .Write(Write), .out_14(_4_bit_Data_Output[3]));
  _2_6_1_memory u_2_6_1_memory_2 (
    .Enable(Enable), .A5(_6_bit_addr[5]), .A4(_6_bit_addr[4]), .A3(_6_bit_addr[3]), .A2(_6_bit_addr[2]),
    .A1(_6_bit_addr[1]), .A0(_6_bit_addr[0]), .R_D(R_D), .S_D(S_D), .Clock(Clock),
    .Data_Write(_4_bit_Data_input[2]), .Read(Read), .Write(Write), .out_14(_4_bit_Data_Output[2]));
  _2_6_1_memory u_2_6_1_memory_3 (
    .Enable(Enable), .A5(_6_bit_addr[5]), .A4(_6_bit_addr[4]), .A3(_6_bit_addr[3]), .A2(_6_bit_addr[2]),
    .A1(_6_bit_addr[1]), .A0(_6_bit_addr[0]), .R_D(R_D), .S_D(S_D), .Clock(Clock),
    .Data_Write(_4_bit_Data_input[1]), .Read(Read), .Write(Write), .out_14(_4_bit_Data_Output[1]));
  _2_6_1_memory u_2_6_1_memory_4 (
    .Enable(Enable), .A5(_6_bit_addr[5]), .A4(_6_bit_addr[4]), .A3(_6_bit_addr[3]), .A2(_6_bit_addr[2]),
    .A1(_6_bit_addr[1]), .A0(_6_bit_addr[0]), .R_D(R_D), .S_D(S_D), .Clock(Clock),
    .Data_Write(_4_bit_Data_input[0]), .Read(Read), .Write(Write), .out_14(_4_bit_Data_Output[0]));
endmodule
